# Fritzing sketch RC car (saved by Fritzing 0.9.3b)

parts:
  M1 = DC Motor
  Part1 = Arduino Uno (Rev3)
  J1 = Basic Servo
  Part2 = NRF24L01+ Breakout Board
  U1 = LIPO-2000mAh [package=lipo-2000]
  IC1 = IC, DIP package, 12 pins [chip_label=ESC]

nets:
  N1: M1.pin_1, IC1.pin2
  N2: M1.pin_2, IC1.pin1
  N3: Part1.D11_PWM/MOSI, Part2.MOSI
  N4: Part1.D12/MISO, Part2.MISO
  N5: Part1.D13/SCK, Part2.SCK
  GND: Part1.GND, J1.gnd, Part2.GND, IC1.pin8
  N6: Part1.D3_PWM, IC1.pin10
  N7: Part1.D4, Part2.CE
  N8: Part1.D5_PWM, Part2.CS
  N9: Part1.D6_PWM, J1.pulse
  3V3: Part1.3V3, Part2.VCC
  N10: Part1.5V, IC1.pin9
  VIN: Part1.VIN, J1.vcc
  N11: U1.+, IC1.pin5
  N12: U1.-, IC1.pin6
